// Logisim project Project.circ as structural Verilog: 1 circuit, main circuit main
module main (
  input  D0,
  input  D1,
  input  D2,
  input  D3,
  input  D4,
  input  D5,
  input  D6,
  input  D7,
  input  D8,
  input  D9,
  input  D10,
  input  D11,
  input  D12,
  input  D13,
  input  D14,
  input  D15,
  input  T0,
  input  T1,
  input  T2,
  input  T3,
  input  T4
);

  wire ar_cont_1_ar_bus, ar_cont_1_ar_inc, ar_cont_1_ar_ld, dr_cont_1_dr_bus, dr_cont_1_dr_inc,
       dr_cont_1_dr_ld, ir_cont_1_ir_bus, ir_cont_1_ir_ld, pc_cont_1_pc_bus, pc_cont_1_pc_inc,
       pc_cont_1_pc_ld;
  wire [3:0] controlled_buffer_1_out, n4_reg_1_out_6, n4_reg_2_out_6, n4_reg_3_out_6, n4_reg_4_out_6;

  AR_Cont ar_cont_1 (
    .D4(D4), .D5(D5), .T0(T0), .T2(T2), .T3(T3), .T4(T4), .AR_BUS(ar_cont_1_ar_bus),
    .AR_INC(ar_cont_1_ar_inc), .AR_LD(ar_cont_1_ar_ld));
  PC_Cont pc_cont_1 (
    .D4(D4), .D5(D5), .D6(D6), .T0(T0), .T1(T1), .T3(T3), .T4(T4), .PC_BUS(pc_cont_1_pc_bus),
    .PC_INC(pc_cont_1_pc_inc), .PC_LD(pc_cont_1_pc_ld));
  DR_Cont dr_cont_1 (
    .D0(D0), .D1(D1), .D2(D2), .T3(T3), .T4(T4), .DR_BUS(dr_cont_1_dr_bus), .DR_INC(dr_cont_1_dr_inc),
    .DR_LD(dr_cont_1_dr_ld));
  IR_Cont ir_cont_1 (.T1(T1), .T2(T2), .IR_BUS(ir_cont_1_ir_bus), .IR_LD(ir_cont_1_ir_ld));
  _4_reg u_4_reg_1 (
    .in_3(controlled_buffer_1_out), .LD(ar_cont_1_ar_ld), .INC(ar_cont_1_ar_inc), .out_6(n4_reg_1_out_6));  // open: CLK, CLR
  _4_reg u_4_reg_2 (
    .in_3(controlled_buffer_1_out), .LD(pc_cont_1_pc_ld), .INC(pc_cont_1_pc_inc), .out_6(n4_reg_2_out_6));  // open: CLK, CLR
  _4_reg u_4_reg_3 (
    .in_3(controlled_buffer_1_out), .LD(dr_cont_1_dr_ld), .INC(dr_cont_1_dr_inc), .out_6(n4_reg_3_out_6));  // open: CLK, CLR
  _4_reg u_4_reg_4 (
    .in_3(controlled_buffer_1_out), .LD(ir_cont_1_ir_ld), .out_6(n4_reg_4_out_6));  // open: CLK, INC, CLR
  assign controlled_buffer_1_out = ar_cont_1_ar_bus ? n4_reg_1_out_6 : 4'bz;  // Controlled_Buffer controlled_buffer_1
  assign controlled_buffer_1_out = pc_cont_1_pc_bus ? n4_reg_2_out_6 : 4'bz;  // Controlled_Buffer controlled_buffer_2
  assign controlled_buffer_1_out = dr_cont_1_dr_bus ? n4_reg_3_out_6 : 4'bz;  // Controlled_Buffer controlled_buffer_3
  assign controlled_buffer_1_out = ir_cont_1_ir_bus ? n4_reg_4_out_6 : 4'bz;  // Controlled_Buffer controlled_buffer_4
endmodule
